# Fritzing sketch Diagram (saved by Fritzing 0.9.3b)
breadboards: 1

parts:
  Part1 = Arduino Uno (Rev3) - ICSP
  ESP01 = ESP8266 WiFi Module [part_number=ESP8266]
  LM317 = Voltage Regulator [package=to220-adj]
  C1 = Electrolytic Capacitor [capacitance=1µF package="100 mil [THT, electrolytic]"]
  C2 = Electrolytic Capacitor [capacitance=1µF package="100 mil [THT, electrolytic]"]
  Part2 = Logic Level Converter
  R1 = Resistor [tolerance=±5% resistance=1k package=THT]
  5V_USB = Power plug
  R2 = Resistor [tolerance=±5% resistance=100 package=THT]
  R3 = Resistor [tolerance=±5% resistance=100 package=THT]
  R4 = Resistor [tolerance=±5% resistance=320 package=THT]

nets:
  GND: Part1.GND, ESP01.GND, C1.-, C2.-, Part2.GND, 5V_USB.GND, R4.Pin_1
  N1: Part1.D6_PWM, Part2.TX_HV
  N2: Part1.D7, Part2.RX_HV
  N3: ESP01.RXD, Part2.RX_LV
  N4: ESP01.VCC, ESP01.CH_PD, LM317.OUT, C1.+, Part2.LV, R1.Pin_0
  N5: ESP01.RST, R1.Pin_1
  N6: ESP01.TXD, Part2.TX_LV
  N7: LM317.ADJ, R2.Pin_1, R4.Pin_0
  N8: LM317.IN, C2.+, Part2.HV, 5V_USB.VCC, R3.Pin_1
  N9: R2.Pin_0, R3.Pin_0

custom parts:
  ESP8266 WiFi Module: Generic WiFi Module based on the ESP8266 with onboard PCB antenna and UART communications
